# Fritzing sketch board (saved by Fritzing 0.9.10b)
breadboards: 1

parts:
  Mod1 = Raspberry Pi Pico W
  A1 = BBAA100043
  Part1 = GY-BMEP280 Barometric Pressure Sensor - Breakout
  Part2 = TM1637

nets:
  N1: Mod1.pin_3, Mod1.pin_8, Mod1.pin_13, Mod1.pin_18, Mod1.pin_23, Mod1.pin_28, Mod1.pin_33, Mod1.pin_38, Mod1.pin_42, A1.pin4, Part1.CSB, Part2.GND
  N2: Mod1.pin_4, A1.pin3
  N3: Mod1.pin_5, A1.pin2
  N4: Mod1.pin_6, A1.pin1
  N5: Mod1.pin_19, Part2.CLK
  N6: Mod1.pin_20, Part2.DIO
  N7: Mod1.pin_21, Part1.SCL
  N8: Mod1.pin_22, Part1.SDA
  N9: Mod1.pin_36, Part1.SDO, Part2.VCC

notes:
  3V3_OUT
  GND
  SCL
  SDA
  VCC
  BMP280

custom parts:
  Raspberry Pi Pico W: Raspberry Pi Pico W. Based around the RP2040 microcontroller the Pico W is a low cost microcontroller device bringing Raspberry Pi quality, cost, and easy of use to the microcontroller space. The areas marked KEEPOUT in pcb silkscreen should not have traces running through them to avoid shorts on a soldered in module!
  BBAA100043: BBAA100043 traffic light module.
  GY-BMEP280 Barometric Pressure Sensor - Breakout: The BME280 is a chip which was originally designed for the next generation of smartphones. It is made up of a very accurate pressure sensor and an associated temperature sensor which helps calibrate the pressure readings. And just for fun they threw in a pretty solid humidity sensor in there as well! So with an I2C connection you have access to enough weather data to make some pretty good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
  TM1637: A 4 7-seg display
